# Fritzing sketch Курсовая (saved by Fritzing 0.9.3b)
breadboards: 1

parts:
  Часть1 = Arduino Uno (Rev3)
  J1 = Piezo Speaker
  Adafruit_HUZZAH_ESP8266_Breakout1 = Adafruit HUZZAH ESP8266 Breakout [part_number=2471]
  LED1 = LED - 5mm [color="Red (633nm)" package="5 mm [THT]"]
  Q1 = PNP-Transistor [package="TO92 [THT]"]
  U1 = Vibration Motor- ROB-08449 [package=vibe-motor-10mm]
  LED3 = DUO LED RG [package="5 mm [THT]"]
  D1 = Rectifier Diode [part_number=1N4001 package="300 mil [THT]"]
  R1 = Resistor [tolerance=±5% resistance=220 package=THT]
  M1 = fc-51 [package=THT]

nets:
  N1: Часть1.D8, R1.Pin_1
  GND: Часть1.D9_PWM, Часть1.D11_PWM/MOSI, Часть1.GND, Adafruit_HUZZAH_ESP8266_Breakout1.GND, Adafruit_HUZZAH_ESP8266_Breakout1.V+#22, Q1.C, U1.-
  N2: Часть1.D5_PWM, LED1.anode
  N3: Часть1.D6_PWM, LED3.green_anode
  N4: J1.pin1, J1.pin2
  N5: Q1.E, D1.cathode
  N6: Q1.B, R1.Pin_0
  N7: M1.pin1, M1.pin2, M1.pin3
